# Fritzing sketch mima-OLED-HAT-01 (saved by Fritzing 0.9.9b)
circuit board: 5.89858cm x 3.56944cm
breadboards: 1

parts:
  LED1-#27 = LED - 3mm [color="Red (633nm)" current=0.030 package="3 mm [THT]"]
  SW-1-#6 = Momentary Switch [package=ksa_sealed_tac_switch]
  SW-2-#5 = Momentary Switch [package=ksa_sealed_tac_switch]
  LED2-#17 = LED - 3mm [color="Red (633nm)" current=0.030 package="3 mm [THT]"]
  Raspberry_Pi1 = Raspberry Pi 2
  R1 = Resistor [tolerance=±5% resistance=2.2k power=0.25 package=THT]
  R2 = Resistor [tolerance=±5% resistance=2.2k power=0.25 package=THT]
  R2_2 = Resistor [tolerance=±5% resistance=2.2k power=0.25 package=THT]
  R1_2 = Resistor [tolerance=±5% resistance=2.2k power=0.25 package=THT]
  R3 = Resistor [tolerance=±5% resistance=1k power=0.25 package=THT]
  R5 = Resistor [tolerance=±5% resistance=220 power=0.25 package=THT]

nets:
  N1: LED1-#27.cathode, LED2-#17.cathode
  N2: LED1-#27.anode, R3.Pin_0
  N3: SW-1-#6.1, SW-1-#6.2, R1.Pin_1, R2.Pin_1
  3V3: SW-1-#6.3, SW-1-#6.4, SW-2-#5.3, SW-2-#5.4, Raspberry_Pi1.3v3, Raspberry_Pi1.3V3
  N4: SW-2-#5.1, SW-2-#5.2, R2_2.Pin_1, R1_2.Pin_1
  N5: LED2-#17.anode, R5.Pin_0
  N6: Raspberry_Pi1.GPIO17, R5.Pin_1
  N7: Raspberry_Pi1.GPIO27, R3.Pin_1
  N8: Raspberry_Pi1.GND, R2.Pin_0, R2_2.Pin_0
  N9: Raspberry_Pi1.GPIO5, R1_2.Pin_0
  N10: Raspberry_Pi1.GPIO6, R1.Pin_0

notes:
  OLED SSD1306
  SCL
  G
  V
  TKJ-seisakusho  mima-OLED-HAT-01
  10
  9
  11
  22
  SDA
  3.3v
  5v
  6
  5
  17
  27
  13
  0
  4
  8
  24
  26
  14
  15
  1
  7
  25
  18
  23
  21
  20
  16
  12
  19
  ●
